# Fritzing sketch ethernet (saved by Fritzing 0.9.4)

parts:
  Bauteil1 = W5100 Ethernet Shield
  Bauteil2 = Arduino Uno (Rev3)

nets:
  GND: Bauteil1.GND, Bauteil2.GND
  N1: Bauteil1.RST, Bauteil2.D9_PWM
  N2: Bauteil1.SCK, Bauteil2.D13/SCK
  N3: Bauteil1.MISO, Bauteil2.D12/MISO
  VCC: Bauteil1.VCC, Bauteil2.5V
  N4: Bauteil1.SS, Bauteil2.D10_PWM/SS
  N5: Bauteil1.MOSI, Bauteil2.D11_PWM/MOSI

custom parts:
  W5100 Ethernet Shield: Mini W5100 Ethernet Shield
